// Logisim project semaforos.circ as structural Verilog: 4 circuits, main circuit Circuito Final
module \Circtuiro_Veículos  (
  input  \Botão_e_Sensor ,
  input  MV,
  output VO,
  output AM,
  output VE
);

  wire and_1_out, clock_1_out, j_k_ff_1_q, j_k_ff_1_qn, j_k_ff_2_q, j_k_ff_2_qn, or_1_out, or_2_out;

  Clock clock_1 (.out(clock_1_out));
  or or_1 (or_1_out, j_k_ff_2_q, \Botão_e_Sensor );
  or or_2 (or_2_out, MV, j_k_ff_2_qn);
  and and_1 (and_1_out, MV, j_k_ff_1_q);
  J_K_Flip_Flop j_k_ff_1 (
    .J(or_1_out), .clk(clock_1_out), .K(or_2_out), .Q(j_k_ff_1_q), .Qn(j_k_ff_1_qn));  // open: preset, en, reset
  J_K_Flip_Flop j_k_ff_2 (
    .J(j_k_ff_1_q), .clk(clock_1_out), .K(and_1_out), .Q(j_k_ff_2_q), .Qn(j_k_ff_2_qn));  // open: preset, en, reset
  and and_2 (VO, j_k_ff_2_q, j_k_ff_1_q);
  xor xor_1 (AM, j_k_ff_2_q, j_k_ff_1_q);
  and and_3 (VE, j_k_ff_2_qn, j_k_ff_1_qn);
endmodule

module \Circuito_Peões  (
  input  \Botão_ou_Sensor ,
  input  in_2,
  output out_3,
  output out_4,
  output out_5,
  output out_6
);

  wire and_1_out, and_2_out, and_3_out, and_4_out, and_5_out, and_6_out, and_7_out, and_8_out, and_9_out,
       and_10_out, and_11_out, and_12_out, and_13_out, and_14_out, and_15_out, and_16_out, and_17_out,
       and_18_out, and_19_out, and_20_out, and_21_out, and_22_out, and_23_out, and_24_out, and_25_out,
       and_26_out, and_27_out, and_28_out, and_29_out, and_30_out, and_31_out, and_32_out, and_33_out,
       and_34_out, clock_1_out, JK0_q, JK0_qn, JK1_q, JK1_qn, JK2_q, JK2_qn, JK3_q, JK3_qn, not_1_out,
       not_2_out, not_3_out, not_4_out, not_5_out, not_6_out, not_7_out, not_8_out, not_9_out, not_10_out,
       not_11_out, not_12_out, not_13_out, not_14_out, not_15_out, not_16_out, not_17_out, or_1_out,
       or_2_out, or_3_out, or_4_out, or_5_out, or_6_out, or_7_out;

  Clock clock_1 (.out(clock_1_out));
  not not_1 (not_1_out, \Botão_ou_Sensor );
  not not_2 (not_2_out, JK0_q);
  not not_3 (not_3_out, JK0_q);
  not not_4 (not_4_out, \Botão_ou_Sensor );
  not not_5 (not_5_out, \Botão_ou_Sensor );
  not not_6 (not_6_out, \Botão_ou_Sensor );
  not not_7 (not_7_out, \Botão_ou_Sensor );
  not not_8 (not_8_out, \Botão_ou_Sensor );
  not not_9 (not_9_out, \Botão_ou_Sensor );
  not not_10 (not_10_out, \Botão_ou_Sensor );
  not not_11 (not_11_out, \Botão_ou_Sensor );
  and and_1 (and_1_out, JK1_q, JK3_qn, not_4_out);
  and and_2 (and_2_out, JK1_qn, JK2_q, not_5_out);
  and and_3 (and_3_out, JK2_qn, JK3_q, not_6_out);
  and and_4 (and_4_out, JK3_q, JK2_qn, \Botão_ou_Sensor );
  and and_5 (and_5_out, JK1_qn, \Botão_ou_Sensor );
  and and_6 (and_6_out, JK3_qn, \Botão_ou_Sensor );
  and and_7 (and_7_out, JK0_q, \Botão_ou_Sensor );
  and and_8 (and_8_out, JK0_q, not_1_out);
  and and_9 (and_9_out, \Botão_ou_Sensor , JK2_q, JK3_q);
  and and_10 (and_10_out, \Botão_ou_Sensor , JK0_q);
  and and_11 (and_11_out, not_2_out, JK3_q, JK2_q);
  and and_12 (and_12_out, not_3_out, JK0_q);
  and and_13 (and_13_out, \Botão_ou_Sensor , JK0_q, JK1_q);
  and and_14 (and_14_out, not_7_out, JK0_q, JK1_q);
  and and_15 (and_15_out, \Botão_ou_Sensor , JK1_q, JK3_q);
  and and_16 (and_16_out, not_8_out, JK1_q, JK3_q);
  and and_17 (and_17_out, \Botão_ou_Sensor , JK0_q, JK1_q);
  and and_18 (and_18_out, not_9_out, JK0_q, JK1_q);
  and and_19 (and_19_out, \Botão_ou_Sensor , JK0_q, JK1_q, JK2_q);
  and and_20 (and_20_out, JK0_q, JK1_q, JK2_q, not_10_out);
  and and_21 (and_21_out, \Botão_ou_Sensor , JK2_q, JK1_q);
  and and_22 (and_22_out, not_11_out, JK2_q, JK1_q);
  or or_1 (or_1_out, and_1_out, and_2_out, and_3_out, and_4_out, and_5_out, and_6_out);
  or or_2 (or_2_out, and_7_out, and_8_out);
  or or_3 (or_3_out, and_9_out, and_10_out, and_11_out, and_12_out);
  or or_4 (or_4_out, and_13_out, and_14_out);
  or or_5 (or_5_out, and_15_out, and_16_out, and_17_out, and_18_out);
  or or_6 (or_6_out, and_19_out, and_20_out);
  or or_7 (or_7_out, and_21_out, and_22_out);
  J_K_Flip_Flop JK0 (.J(or_1_out), .clk(clock_1_out), .K(in_2), .Q(JK0_q), .Qn(JK0_qn));  // open: preset, en, reset
  J_K_Flip_Flop JK1 (.J(or_2_out), .clk(clock_1_out), .K(or_3_out), .Q(JK1_q), .Qn(JK1_qn));  // open: preset, en, reset
  J_K_Flip_Flop JK2 (.J(or_4_out), .clk(clock_1_out), .K(or_5_out), .Q(JK2_q), .Qn(JK2_qn));  // open: preset, en, reset
  J_K_Flip_Flop JK3 (.J(or_6_out), .clk(clock_1_out), .K(or_7_out), .Q(JK3_q), .Qn(JK3_qn));  // open: preset, en, reset
  not not_12 (not_12_out, \Botão_ou_Sensor );
  not not_13 (not_13_out, \Botão_ou_Sensor );
  not not_14 (not_14_out, \Botão_ou_Sensor );
  not not_15 (not_15_out, \Botão_ou_Sensor );
  not not_16 (not_16_out, \Botão_ou_Sensor );
  not not_17 (not_17_out, \Botão_ou_Sensor );
  and and_23 (and_23_out, \Botão_ou_Sensor , JK2_qn, JK3_q);
  and and_24 (and_24_out, \Botão_ou_Sensor , JK2_q, JK3_qn);
  and and_25 (and_25_out, not_12_out, JK2_qn, JK3_q);
  and and_26 (and_26_out, not_13_out, JK2_q, JK3_qn);
  and and_27 (and_27_out, \Botão_ou_Sensor , JK1_q, JK2_q, JK3_q);
  and and_28 (and_28_out, \Botão_ou_Sensor , JK3_qn, JK2_qn);
  and and_29 (and_29_out, not_15_out, JK1_q, JK2_q, JK3_q);
  and and_30 (and_30_out, not_16_out, JK3_qn, JK2_qn);
  and and_31 (and_31_out, \Botão_ou_Sensor , JK1_qn, JK2_q, JK3_q);
  and and_32 (and_32_out, not_17_out, JK1_qn, JK2_q, JK3_q);
  and and_33 (and_33_out, \Botão_ou_Sensor , JK1_q, JK2_q, JK3_q);
  and and_34 (and_34_out, not_14_out, JK1_q, JK2_q, JK3_q);
  or or_8 (out_3, and_27_out, and_28_out, and_29_out, and_30_out);
  or or_9 (out_4, and_31_out, and_32_out);
  or or_10 (out_5, and_23_out, and_24_out, and_25_out, and_26_out);
  or or_11 (out_6, and_33_out, and_34_out);
endmodule

module Display_7_segmentos (
  input  in_1,
  output out_2,
  output out_3,
  output out_4,
  output out_5,
  output out_6,
  output out_7,
  output out_8
);

  wire and_1_out, and_2_out, and_3_out, and_4_out, and_5_out, and_6_out, and_7_out, and_8_out, and_9_out,
       clock_1_out, j_k_ff_1_q, j_k_ff_1_qn, j_k_ff_2_q, j_k_ff_2_qn, j_k_ff_3_q, j_k_ff_3_qn, xor_1_out,
       xor_2_out;

  Clock clock_1 (.out(clock_1_out));
  and and_1 (and_1_out, j_k_ff_2_q, j_k_ff_1_q);
  J_K_Flip_Flop j_k_ff_1 (
    .J(in_1), .clk(clock_1_out), .K(in_1), .Q(j_k_ff_1_q), .Qn(j_k_ff_1_qn));  // open: preset, en, reset
  J_K_Flip_Flop j_k_ff_2 (
    .J(j_k_ff_1_q), .clk(clock_1_out), .K(j_k_ff_1_q), .Q(j_k_ff_2_q), .Qn(j_k_ff_2_qn));  // open: preset, en, reset
  J_K_Flip_Flop j_k_ff_3 (
    .J(and_1_out), .clk(clock_1_out), .K(and_1_out), .Q(j_k_ff_3_q), .Qn(j_k_ff_3_qn));  // open: preset, en, reset
  xor xor_1 (xor_1_out, j_k_ff_2_q, j_k_ff_1_q);
  and and_2 (and_2_out, j_k_ff_2_qn, j_k_ff_1_q, j_k_ff_3_q);
  and and_3 (and_3_out, j_k_ff_3_qn, j_k_ff_1_qn);
  and and_4 (and_4_out, j_k_ff_3_qn, j_k_ff_2_q);
  and and_5 (and_5_out, j_k_ff_2_q, j_k_ff_1_qn);
  and and_6 (and_6_out, j_k_ff_1_qn, j_k_ff_2_q);
  and and_7 (and_7_out, j_k_ff_1_qn, j_k_ff_3_qn);
  and and_8 (and_8_out, j_k_ff_1_qn, j_k_ff_2_qn);
  and and_9 (and_9_out, j_k_ff_3_qn, j_k_ff_2_q);
  xor xor_2 (xor_2_out, j_k_ff_3_q, j_k_ff_2_q);
  or or_1 (out_2, xor_1_out, j_k_ff_3_qn);
  or or_2 (out_3, j_k_ff_3_q, j_k_ff_2_qn);
  or or_3 (out_4, j_k_ff_1_q, j_k_ff_3_qn, j_k_ff_2_qn);
  or or_4 (out_5, and_2_out, and_3_out, and_4_out, and_5_out);
  or or_5 (out_6, and_6_out, and_7_out);
  or or_6 (out_7, and_8_out, and_9_out);
  or or_7 (out_8, xor_2_out, j_k_ff_1_qn);
endmodule

module Circuito_Final (
  input  in_1
);

  wire \circtuiro_veículos_1_am , \circtuiro_veículos_1_ve , \circtuiro_veículos_1_vo ,
       \circuito_peões_1_out_3 , \circuito_peões_1_out_4 , \circuito_peões_1_out_5 ,
       \circuito_peões_1_out_6 , display_7_segmentos_1_out_2, display_7_segmentos_1_out_3,
       display_7_segmentos_1_out_4, display_7_segmentos_1_out_5, display_7_segmentos_1_out_6,
       display_7_segmentos_1_out_7, display_7_segmentos_1_out_8;

  \Circtuiro_Veículos  \circtuiro_veículos_1  (
    .\Botão_e_Sensor (in_1), .MV(\circuito_peões_1_out_6 ), .VO(\circtuiro_veículos_1_vo ),
    .AM(\circtuiro_veículos_1_am ), .VE(\circtuiro_veículos_1_ve ));
  \Circuito_Peões  \circuito_peões_1  (
    .in_2(in_1), .\Botão_ou_Sensor (in_1), .out_3(\circuito_peões_1_out_3 ),
    .out_4(\circuito_peões_1_out_4 ), .out_5(\circuito_peões_1_out_5 ), .out_6(\circuito_peões_1_out_6 ));
  LED led_1 (.in(\circtuiro_veículos_1_vo ));
  LED led_2 (.in(\circtuiro_veículos_1_am ));
  LED led_3 (.in(\circtuiro_veículos_1_ve ));
  LED led_4 (.in(\circuito_peões_1_out_3 ));
  LED led_5 (.in(\circuito_peões_1_out_4 ));
  LED led_6 (.in(\circuito_peões_1_out_5 ));
  Display_7_segmentos display_7_segmentos_1 (
    .in_1(\circuito_peões_1_out_5 ), .out_2(display_7_segmentos_1_out_2),
    .out_3(display_7_segmentos_1_out_3), .out_4(display_7_segmentos_1_out_4),
    .out_5(display_7_segmentos_1_out_5), .out_6(display_7_segmentos_1_out_6),
    .out_7(display_7_segmentos_1_out_7), .out_8(display_7_segmentos_1_out_8));
  _7_Segment_Display u_7_segment_display_1 (
    .g(display_7_segmentos_1_out_8), .f(display_7_segmentos_1_out_7), .a(display_7_segmentos_1_out_2),
    .b(display_7_segmentos_1_out_3), .e(display_7_segmentos_1_out_6), .d(display_7_segmentos_1_out_5),
    .c(display_7_segmentos_1_out_4));  // open: dp
endmodule
